# Fritzing sketch btn_gpio (saved by Fritzing 0.9.2b)
breadboards: 1

parts:
  Raspberry_Pi1 = Raspberry Pi 2
  R1 = Resistor [tolerance=±5% resistance=330 package=THT]
  LED1 = LED - 5mm [color="Red (633nm)" package="5 mm [THT]"]
  LED2 = LED - 5mm [color="Yellow (595nm)" package="5 mm [THT]"]
  R2 = Resistor [tolerance=±5% resistance=330 package=THT]
  LED3 = LED - 5mm [color="Green (555nm)" package="5 mm [THT]"]
  R3 = Resistor [tolerance=±5% resistance=330 package=THT]
  S1 = Pushbutton [package="[THT]"]

nets:
  N1: Raspberry_Pi1.3v3, R1.Pin_0, LED1.cathode
  N2: Raspberry_Pi1.GND, R1.Pin_1, R2.Pin_1, R3.Pin_1, S1.Pin_3, S1.Pin_4
  N3: Raspberry_Pi1.GPIO17, LED1.anode
  N4: Raspberry_Pi1.GPIO27, LED2.anode
  N5: Raspberry_Pi1.GPIO22, LED3.anode
  N6: Raspberry_Pi1.GPIO16, S1.Pin_1, S1.Pin_2
  N7: LED2.cathode, R2.Pin_0
  N8: LED3.cathode, R3.Pin_0
