# Fritzing sketch led_gpio (saved by Fritzing 0.9.2b)
breadboards: 1

parts:
  Raspberry_Pi1 = Raspberry Pi 2
  R1 = Resistor [tolerance=±5% resistance=330 package=THT]
  LED1 = LED - 5mm [color="Red (633nm)" package="5 mm [THT]"]

nets:
  N1: Raspberry_Pi1.3v3, R1.Pin_0, LED1.cathode
  N2: Raspberry_Pi1.GND, R1.Pin_1
  N3: Raspberry_Pi1.GPIO17, LED1.anode
